# Fritzing sketch Automatic Keypad Energy Meter Recharge V2 (saved by Fritzing 0.8.7b)
breadboards: 1

parts:
  J2 = Basic Servo
  M3 = Stepper Motor - Bipolar  # not connected
  M4 = Stepper Motor - Bipolar  # not connected
  L298N3 = L298N DC motor driver
  L298N4 = L298N DC motor driver
  BAT2 = BC9VPC [package=bc9vpc]
  VCC2 = Battery
  U1 = ESP8266 NodeMCU LoLin module

nets:
  GND: J2.gnd, L298N3.GND, L298N4.12V, BAT2.V-, VCC2.-, U1.GND
  VCC: J2.vcc, VCC2.+, U1.Vin
  12V: L298N3.12V, L298N4.GND, BAT2.V+
  N1: L298N3.IN1, U1.D1
  N2: L298N3.IN2, U1.D2
  N3: L298N3.IN3, U1.D5
  N4: L298N3.IN4, U1.D6
  N5: L298N4.IN1, U1.D7
  N6: L298N4.IN2, U1.D8
  N7: L298N4.IN3, U1.D3
  N8: L298N4.IN4, U1.D4

custom parts:
  L298N DC motor driver: 2x DC motor driver with 78M05 positive voltage regulator (7..35 V) L298N: max 46 V, 2 A Set 5 V Enable jumper to enable 5 V regultor (needed for the L298N) and +5 V output at screw terminal or supply external +5 V at screw terminal Set ENA and/or ENB to +5 V to enable motor permanently or supply ENA and/or ENB with PWM signal IN1 and IN2 set rotation directory for motor A (OUT1/OUT2) IN2 and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
  ESP8266 NodeMCU LoLin module: ESP8266 based NodeMCU
